# Fritzing sketch roboSumoSimples (saved by Fritzing 0.9.3b)
breadboards: 1

parts:
  U1 = L9110 H-bridge module [part_number="L9110 H-bridge"]
  Componente1 = Arduino Mega 2560 (Rev3)
  U2 = BATTERY-2 [package=battery-aaa]
  U3 = BATTERY-2 [package=battery-aaa]
  U4 = BATTERY-2 [package=battery-aaa]
  U5 = BATTERY-2 [package=battery-aaa]
  HC-SR04_Sensor_1 = HC-SR04 Ultrasonic Distance Sensor
  U6 = BATTERY-2 [package=battery-aaa]
  U7 = BATTERY-2 [package=battery-aaa]
  U8 = BATTERY-2 [package=battery-aaa]
  U9 = BATTERY-2 [package=battery-aaa]
  M1 = fc-51 [package=THT]
  MOTOR_DC_6V_direito1 = MOTOR_DC6V
  Motor_DC_Esquerdo1 = Motor DC 6V Esquerdo

nets:
  N1: U1.B-IA, Componente1.D8_PWM
  N2: U1.B-IB, Componente1.D9_PWM
  N3: U1.VCC, U5.-1
  N4: U1.A-IA, Componente1.D10_PWM
  N5: U1.A-IB, Componente1.D11_PWM
  N6: U1.MOTOR_A-A, Motor_DC_Esquerdo1.GND
  N7: U1.MOTOR_A-B, Motor_DC_Esquerdo1.VCC
  N8: U1.MOTOR_B-A, MOTOR_DC_6V_direito1.GND
  N9: U1.MOTOR_B-B, MOTOR_DC_6V_direito1.VCC
  N10: Componente1.A0, M1.pin1
  5V: Componente1.5V, HC-SR04_Sensor_1.VCC, M1.pin3
  GND: Componente1.GND, HC-SR04_Sensor_1.GND, U8.+1, M1.pin2
  N11: Componente1.VIN, U6.-1
  N12: Componente1.D6_PWM, HC-SR04_Sensor_1.ECHO
  N13: Componente1.D7_PWM, HC-SR04_Sensor_1.TRIG
  N14: U2.-1, U3.+1
  N15: U3.-1, U4.+1
  N16: U4.-1, U5.+1
  N17: U6.+1, U9.-1
  N18: U7.-1, U9.+1
  N19: U7.+1, U8.-1

custom parts:
  MOTOR_DC6V: Motor dc 6V direito
  Motor DC 6V Esquerdo: Motor dc esquerdo
